# Fritzing sketch Lab2-HardWiredPushbutton2 (saved by Fritzing 0.9.2b)
breadboards: 1

parts:
  T-Cobbler1 = T-Cobbler
  LED1 = LED - 5mm [color="Red (633nm)" package="5 mm [THT]"]
  R1 = Resistor [tolerance=±5% resistance=470 package=THT]
  S1 = Momentary Switch [package=ksa_sealed_tac_switch]

nets:
  N1: T-Cobbler1.3V3#0, S1.1
  N2: T-Cobbler1.GND#4, R1.Pin_1
  N3: LED1.cathode, R1.Pin_0
  N4: LED1.anode, S1.3

custom parts:
  T-Cobbler: T-Cobbler for RPi B+ and Rpi2 from SunFounder
