# Fritzing sketch Lab3-FlashingLED2 (saved by Fritzing 0.9.2b)
breadboards: 1

parts:
  T-Cobbler1 = T-Cobbler
  LED1 = LED - 5mm [color="Red (633nm)" package="5 mm [THT]"]
  R1 = Resistor [tolerance=±5% resistance=470 package=THT]

nets:
  N1: T-Cobbler1.GND#4, R1.Pin_1
  N2: T-Cobbler1.GPIO16, LED1.anode
  N3: LED1.cathode, R1.Pin_0

custom parts:
  T-Cobbler: T-Cobbler for RPi B+ and Rpi2 from SunFounder
