# Fritzing sketch Lab4-PushbuttonInput2 (saved by Fritzing 0.9.2b)
breadboards: 1

parts:
  T-Cobbler1 = T-Cobbler
  LED1 = LED - 5mm [color="Red (633nm)" package="5 mm [THT]"]
  R1 = Resistor [tolerance=±5% resistance=470 package=THT]
  S1 = Momentary Switch [package=ksa_sealed_tac_switch]

nets:
  N1: T-Cobbler1.GND#4, R1.Pin_1, S1.2
  N2: T-Cobbler1.GPIO18, S1.3
  N3: T-Cobbler1.GPIO16, LED1.anode
  N4: LED1.cathode, R1.Pin_0

custom parts:
  T-Cobbler: T-Cobbler for RPi B+ and Rpi2 from SunFounder
