# Fritzing sketch LabChallenge1-SingleTrafficStop2 (saved by Fritzing 0.9.2b)
breadboards: 1

parts:
  T-Cobbler1 = T-Cobbler
  R1 = Resistor [tolerance=±5% resistance=470 package=THT]
  LED2 = LED - 5mm [color="Red (633nm)" package="5 mm [THT]"]
  R2 = Resistor [tolerance=±5% resistance=470 package=THT]
  LED3 = LED - 5mm [color="Yellow (585nm)" package="5 mm [THT]"]
  LED4 = LED - 5mm [color="Green (565nm)" package="5 mm [THT]"]
  R3 = Resistor [tolerance=±5% resistance=470 package=THT]

nets:
  N1: T-Cobbler1.GND#4, R1.Pin_1, R2.Pin_1, R3.Pin_1
  N2: T-Cobbler1.GPIO16, LED2.anode
  N3: T-Cobbler1.GPIO20, LED3.anode
  N4: T-Cobbler1.GPIO21, LED4.anode
  N5: R1.Pin_0, LED2.cathode
  N6: R2.Pin_0, LED3.cathode
  N7: LED4.cathode, R3.Pin_0

custom parts:
  T-Cobbler: T-Cobbler for RPi B+ and Rpi2 from SunFounder
