# Fritzing sketch LabChallenge3-TwoTrafficStopWithCrosswalk2 (saved by Fritzing 0.9.2b)
breadboards: 1

parts:
  T-Cobbler1 = T-Cobbler
  R1 = Resistor [tolerance=±5% resistance=470 package=THT]
  LED2 = LED - 5mm [color="Red (633nm)" package="5 mm [THT]"]
  R2 = Resistor [tolerance=±5% resistance=470 package=THT]
  LED3 = LED - 5mm [color="Yellow (585nm)" package="5 mm [THT]"]
  LED4 = LED - 5mm [color="Green (565nm)" package="5 mm [THT]"]
  R3 = Resistor [tolerance=±5% resistance=470 package=THT]
  LED5 = LED - 5mm [color="Red (633nm)" package="5 mm [THT]"]
  LED6 = LED - 5mm [color="Yellow (585nm)" package="5 mm [THT]"]
  LED7 = LED - 5mm [color="Green (565nm)" package="5 mm [THT]"]
  R4 = Resistor [tolerance=±5% resistance=470 package=THT]
  R5 = Resistor [tolerance=±5% resistance=470 package=THT]
  R6 = Resistor [tolerance=±5% resistance=470 package=THT]
  LED8 = LED - 5mm [color="White (8000K)" package="5 mm [THT]"]
  LED9 = LED - 5mm [color="White (8000K)" package="5 mm [THT]"]
  S1 = Momentary Switch [package=ksa_sealed_tac_switch]
  S2 = Momentary Switch [package=ksa_sealed_tac_switch]
  R7 = Resistor [tolerance=±5% resistance=470k package=THT]
  R8 = Resistor [tolerance=±5% resistance=470k package=THT]

nets:
  N1: T-Cobbler1.GND#4, R1.Pin_1, R2.Pin_1, R3.Pin_1, R6.Pin_1, S1.4, S2.4, R7.Pin_1, R8.Pin_1
  N2: T-Cobbler1.GPIO22, S2.1
  N3: T-Cobbler1.GPIO5, LED9.anode
  N4: T-Cobbler1.GPIO13, LED5.anode
  N5: T-Cobbler1.GPIO19, LED6.anode
  N6: T-Cobbler1.GPIO26, LED7.anode
  N7: T-Cobbler1.GPIO18, S1.1
  N8: T-Cobbler1.GPIO12, LED8.anode
  N9: T-Cobbler1.GPIO16, LED2.anode
  N10: T-Cobbler1.GPIO20, LED3.anode
  N11: T-Cobbler1.GPIO21, LED4.anode
  N12: R1.Pin_0, LED2.cathode
  N13: R2.Pin_0, LED3.cathode
  N14: LED4.cathode, R3.Pin_0
  N15: LED5.cathode, R4.Pin_0
  N16: LED6.cathode, R6.Pin_0
  N17: LED7.cathode, R5.Pin_0
  N18: LED8.cathode, R7.Pin_0
  N19: LED9.cathode, R8.Pin_0

custom parts:
  T-Cobbler: T-Cobbler for RPi B+ and Rpi2 from SunFounder
